# Fritzing sketch magpi (saved by Fritzing 0.8.6b)

parts:
  S1 = Pushbutton [package="[THT]"]
  S2 = Pushbutton [package="[THT]"]
  S3 = Pushbutton [package="[THT]"]
  S4 = Pushbutton [package="[THT]"]
  S5 = Pushbutton [package="[THT]"]
  S6 = Pushbutton [package="[THT]"]
  S7 = Pushbutton [package="[THT]"]
  Part1 = Arduino Pro Mini v13
  Part2 = USB LiPoly Charger
  U1 = SWITCH_SPDT [package=kps-1290]
  U2 = LIPO-110mAh [package=lipo-110]
  Nokia_5110_LCD_Module3 = nokia5110

nets:
  N1: S1.Pin_2, Part1.A0
  GND: S1.Pin_3, S2.Pin_3, S2.Pin_4, S3.Pin_3, S3.Pin_4, S4.Pin_3, S5.Pin_3, S5.Pin_4, S6.Pin_3, S6.Pin_4, S7.Pin_3, Part1.GND, Part2.GND, U2.-, Nokia_5110_LCD_Module3.1_GND
  N2: S2.Pin_2, Part1.D13/SCK
  N3: S3.Pin_2, Part1.D12/MISO
  N4: S4.Pin_1, S4.Pin_2, Part1.D11_PWM/MOSI
  N5: S5.Pin_1, S5.Pin_2, Part1.D10_PWM/SS
  N6: S6.Pin_1, S6.Pin_2, Part1.D7
  N7: S7.Pin_2, Part1.D8
  N8: Part1.RAW, U1.O
  N9: Part1.VCC, Nokia_5110_LCD_Module3.2_Vcc
  N10: Part1.D9_PWM, Nokia_5110_LCD_Module3.8_LED
  N11: Part1.D6_PWM, Nokia_5110_LCD_Module3.7_RST
  N12: Part1.D5_PWM, Nokia_5110_LCD_Module3.6_CS
  N13: Part1.D4, Nokia_5110_LCD_Module3.5_D/C
  N14: Part1.D3_PWM, Nokia_5110_LCD_Module3.4_DIN
  N15: Part1.D2, Nokia_5110_LCD_Module3.3_SCLK
  N16: Part2.VBAT, U1.P, U2.+

custom parts:
  : Nokia 5110 LCD with 8 pin. It's a 45mm*45mm module part. Description: The Nokia 5110 is a basic graphic LCD screen for lots of applications. It was originally intended for as a cell phone screen. This one is mounted on an easy to solder PCB. It uses the PCD8544 controller. The PCD8544 is a low power CMOS LCD controller/driver, designed to drive a graphic display of 48 rows and 84 columns. All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
